# Fritzing sketch ArduinoNanoSketch (saved by Fritzing 0.9.3b)
circuit board: 8.46667cm x 5.64444cm
breadboards: 1

parts:
  Arduino = Arduino Nano (Rev3.0)
  D1 = Rectifier Diode [part_number=1N4001 package="300 mil [THT]"]
  R1 = Resistor [tolerance=±5% resistance=330 package=THT]
  Q1 = NPN-Transistor [package="TO92 [THT]"]
  Q2 = NPN-Transistor [package="TO92 [THT]"]
  L1 = Solenoid
  C2 = Electrolytic Capacitor [capacitance=100µF voltage=16V package="100 mil [THT, electrolytic]"]
  Piezo = Microphone
  Power_plug1 = Power plug  # not connected

nets (from the pcb view):
  N1: Arduino.GND, Q1.C, Q2.C
  N2: Arduino.D5, Q2.B
  N3: Arduino.D9, Q1.B
  N4: Arduino.VIN, L1.pin2
  N5: Arduino.A0, D1.cathode, C2.-
  N6: D1.anode, Piezo.pin2
  N7: R1.Pin_1, Q1.E
  N8: Q2.E, L1.pin1
  N9: C2.+, Piezo.pin1

notes:
  Piezoelectricity
  valve
  6V

// code stored in the sketch: PiezoAsASwitch.ino
const int VALVE_SWITCH = 9;
const int UNLOAD_SWITCH = 5;

// the setup function runs once when you press reset or power the board
void setup() {
  // initialize digital pin LED_BUILTIN as an output.
  pinMode(LED_BUILTIN, OUTPUT);
  pinMode(VALVE_SWITCH, OUTPUT);
  pinMode(UNLOAD_SWITCH, OUTPUT);

  Serial.begin(9600);
}

// the loop function runs over and over again forever
void loop() {
  int piezoADC = analogRead(A0);
  Serial.println(piezoADC);

  if (piezoADC > 20) {
    digitalWrite(LED_BUILTIN, HIGH);   // turn the LED on (HIGH is the voltage level)
    digitalWrite(VALVE_SWITCH, HIGH);
    digitalWrite(UNLOAD_SWITCH, HIGH);
    delay(5000);
  } else {
    digitalWrite(LED_BUILTIN, LOW);    // turn the LED off by making the voltage LOW
    digitalWrite(VALVE_SWITCH, LOW);
    digitalWrite(UNLOAD_SWITCH, LOW);
    delay(1000);
  }
}
